# Fritzing sketch Automated Rice Dispenser (saved by Fritzing 0.9.3b)
breadboards: 1

parts:
  Arduino_Uno_Rev_3 = Arduino Uno (Rev3)
  Water_Dispensing_Valve = Solenoid
  Hi_Tec_HB_785 = Basic Servo
  5v_1A_DC_Input = DC Power [voltage=5]
  Water_Dispensing_Valve_Relay = RELAY-SOLIDSTATE [package=relay-s108t02]
  Water_Dispenser_Enable_Switch = SPST Switch [package=switch-spdt]

nets:
  N1: Arduino_Uno_Rev_3.A0, Water_Dispenser_Enable_Switch.S
  N2: Arduino_Uno_Rev_3.D9_PWM, Hi_Tec_HB_785.pulse
  N3: Arduino_Uno_Rev_3.D10_PWM/SS, Water_Dispensing_Valve_Relay.T1
  N4: Arduino_Uno_Rev_3.D11_PWM/MOSI, Water_Dispensing_Valve_Relay.T2
  N5: Arduino_Uno_Rev_3.5V, Water_Dispenser_Enable_Switch.P
  GND: Arduino_Uno_Rev_3.GND, Water_Dispensing_Valve.pin2, Hi_Tec_HB_785.gnd, 5v_1A_DC_Input.V-
  VIN: Arduino_Uno_Rev_3.VIN, Hi_Tec_HB_785.vcc, 5v_1A_DC_Input.V+, Water_Dispensing_Valve_Relay.+
  N6: Water_Dispensing_Valve.pin1, Water_Dispensing_Valve_Relay.-
